# Fritzing sketch TLCv1 (saved by Fritzing 0.9.3b)
circuit board: 6.5cm x 4.5cm
breadboards: 1

parts:
  <--_Status = RGB LED (com. cathode, rbg) [package="5 mm [THT]"]
  Effect_Toggle = Header 2 [package=molex-1x2_lock]
  Pwr_Swtch = Header 2 [package=molex-1x2_lock]
  Power_5-12v = Header 2 [package=molex-1x2_lock]
  Config = DIP Switch 4 Position [package=dipswitch-04]
  5v_or_3_3v = female pin header, 3 pins [form="♀ (female)"]
  LED_Strip = Header 3 [package=molex-1x3_lock]
  100uf = Capacitor Polarized [package=cpol-radial-100uf-25v]
  Pulse_Sensor_-> = Header 3 [package=molex-1x3_lock]
  Nano = Arduino Nano (Rev3.0)
  nRF24L01 = Generic shrouded header - 8 pins [form="♂ (shrouded male)" package=THT]
  R1 = Resistor [tolerance=±5% resistance=220 package=THT]
  R2 = Resistor [tolerance=±5% resistance=220 package=THT]
  R3 = Resistor [tolerance=±5% resistance=220 package=THT]
  J2 = female pin header, 7 pins [form="♀ (female)"]

nets:
  N1: <--_Status.red_anode, R3.Pin_1
  N2: <--_Status.common_cathode, Effect_Toggle.2, Power_5-12v.2, Config.5, Config.6, Config.7, Config.8, LED_Strip.3, 100uf.-, Pulse_Sensor_->.1, Nano.GND, nRF24L01.grd
  N3: <--_Status.blue_anode, R1.Pin_1
  N4: <--_Status.green_anode, R2.Pin_1
  N5: Effect_Toggle.1, Nano.D6
  N6: Pwr_Swtch.1, Nano.VIN
  N7: Pwr_Swtch.2, Power_5-12v.1
  N8: Config.1, Nano.D2
  N9: Config.2, Nano.D3
  N10: Config.3, Nano.D4
  N11: Config.4, Nano.D5
  N12: 5v_or_3_3v.pin1, Nano.3V3, J2.pin6
  N13: 5v_or_3_3v.pin2, 100uf.+, nRF24L01.v+
  N14: 5v_or_3_3v.pin3, LED_Strip.1, Pulse_Sensor_->.2, Nano.5V, J2.pin7
  N15: LED_Strip.2, Nano.D8
  N16: Pulse_Sensor_->.3, Nano.A7
  N17: Nano.D7, J2.pin1
  N18: Nano.D9, nRF24L01.ce
  N19: Nano.D10, nRF24L01.csn
  N20: Nano.D11/MOSI, nRF24L01.mosi
  N21: Nano.D12/MISO, nRF24L01.miso
  N22: Nano.A6, J2.pin5
  N23: Nano.A5, J2.pin4
  N24: Nano.A4, J2.pin3
  N25: Nano.A3, J2.pin2
  N26: Nano.A2, R2.Pin_0
  N27: Nano.A1, R1.Pin_0
  N28: Nano.A0, R3.Pin_0
  N29: Nano.D13/SCK, nRF24L01.sck

notes:
  Totally Legit Camp: Terrific LED Controller
  hecho en mexico

custom parts:
  Generic shrouded header - 8 pins: Generic shrouded header
