# Fritzing sketch Untitled Sketch 2 (saved by Fritzing 0.9.3b)
circuit board: 5.9686cm x 3.13291cm
breadboards: 1

parts:
  R1 = Resistor [tolerance=±5% resistance=220 package=THT]
  part = Arduino Nano (Rev3.0)
  LED1 = RGB LED (com. cathode, rbg) [package="5 mm [THT]"]
  C1 = Capacitor Polarized [package=cpol-radial-100uf-25v]  # not connected

nets:
  N1: R1.Pin_0, LED1.common_cathode
  N2: R1.Pin_1, part.GND
  N3: part.D2, LED1.red_anode
  N4: part.D3, LED1.blue_anode
  N5: part.D4, LED1.green_anode
